// Logisim project RAIYAN_MASOOD_HRIDDHO_1931117042_CSE_332_LAB_SECTION_NO_01_ASSIGNMENT_NO_01_SUMMER_2023_SEMESTER.circ as structural Verilog: 2 circuits, main circuit main
module main (
  input  [7:0] A,
  input  [7:0] B,
  input  [2:0] S,
  output [7:0] Y
);

  wire [7:0] and_1_out, nand_1_out, not_1_out, not_2_out, or_1_out, xor_1_out;

  assign nand_1_out = ~(B & A);  // NAND_Gate nand_1, 8 bits wide
  assign or_1_out = B | A;  // OR_Gate or_1, 8 bits wide
  assign and_1_out = B & A;  // AND_Gate and_1, 8 bits wide
  assign xor_1_out = B ^ A;  // XOR_Gate xor_1, 8 bits wide
  assign not_1_out = ~A;  // NOT_Gate not_1, 8 bits wide
  assign not_2_out = ~B;  // NOT_Gate not_2, 8 bits wide
  Multiplexer #(.select(3), .width(8)) multiplexer_1 (
    .in0(nand_1_out), .in1(or_1_out), .in2(and_1_out), .in3(xor_1_out), .in4(not_1_out), .in5(not_2_out),
    .out(Y), .sel(S));  // open: in6, in7
endmodule

module circ2 (
  input  [7:0] in_1,
  input  [7:0] in_2,
  input  [2:0] in_3,
  output [7:0] out_4
);

  main main_1 (.A(in_1), .B(in_2), .S(in_3), .Y(out_4));
endmodule
